# Fritzing sketch Arduino Clock (saved by Fritzing 0.9.1b)

parts:
  IC1 = DS1307 [package=THT]
  SPKR1 = Loudspeaker
  Part1 = Arduino Uno (Rev3) - ICSP
  T1 = TMP36 Temperature Sensor [package="TO92 [THT]"]
  U1 = HIH-4030 [package=hih-4030]
  7SEG1 = 7-Segment LED I2C Backpack (red)
  7SEG2 = 7-Segment LED I2C Backpack (green)
  7SEG3 = 7-Segment LED I2C Backpack (yellow)
  S1 = Round Pushbutton
  S2 = Round Pushbutton
  S3 = Round Pushbutton
  S4 = SPST Switch [package=r_sw_th]
  C2 = Capacitor [package=cap-pth-small2]
  Part2 = LilyPad Coin Cell Battery Holder
  Y1 = CRYSTAL [package=tc26h]
  D1 = Rectifier Diode [part_number=1N4001 package="300 mil [THT]"]
  C3 = Capacitor Polarized [package=cpol-radial-10uf-25v]
  R1 = Resistor [tolerance=±5% resistance=4.7 package="0805 [SMD]"]
  R2 = Resistor [tolerance=±5% resistance=4.7 package="0805 [SMD]"]
  C4 = Capacitor [package=cap-pth-small2]
  R3 = Resistor [tolerance=±5% resistance=80k package="0805 [SMD]"]
  R4 = Resistor [tolerance=±5% resistance=10k package="0805 [SMD]"]
  R5 = Resistor [tolerance=±5% resistance=10k package="0805 [SMD]"]
  R6 = Resistor [tolerance=±5% resistance=10k package="0805 [SMD]"]
  R7 = Resistor [tolerance=±5% resistance=10k package="0805 [SMD]"]
  R8 = Resistor [tolerance=±5% resistance=150 package="0805 [SMD]"]

nets:
  N1: IC1.X1_-_Crystal, Y1.1
  N2: IC1.X2_-_Crystal, Y1.2
  N3: IC1.Vbat_-_Backup_Supply, Part2.+
  N4: IC1.0V, Part2.-
  N5: IC1.SDA_-_I2C_Data, Part1.ICSP_MOSI, Part1.D11_PWM/MOSI, 7SEG1.SDA, 7SEG2.SDA, 7SEG3.SDA, R2.Pin_1
  N6: IC1.SCL_-_I2C_Clock, Part1.A5/SCL, 7SEG1.SCL, 7SEG2.SCL, 7SEG3.SCL, R1.Pin_1
  N7: IC1.+V, C4.2
  N8: SPKR1.pin1, C3.-
  GND: SPKR1.pin2, Part1.GND, T1.GND, U1.GND, 7SEG1.GND, 7SEG2.GND, 7SEG3.GND, S4.S, C2.2, C4.1, R3.Pin_1, R4.Pin_1, R5.Pin_1, R6.Pin_1, R7.Pin_1
  N9: Part1.A0, T1.Vout
  N10: Part1.A1, U1.OUT
  N11: Part1.ICSP_MISO, Part1.D12/MISO, D1.anode
  5V: Part1.5V, T1.+Vs, U1.VCC, 7SEG1.V+, 7SEG2.V+, 7SEG3.V+, S1.leg1, S2.leg0, S3.leg0, S4.O, C2.1, R1.Pin_0, R2.Pin_0, R3.Pin_0
  N12: Part1.D2, S1.leg0, R4.Pin_0
  N13: Part1.D3_PWM, S3.leg1, R5.Pin_0
  N14: Part1.D4, S2.leg1, R6.Pin_0
  N15: Part1.D5_PWM, S4.P, R7.Pin_0
  N16: D1.cathode, R8.Pin_0
  N17: C3.+, R8.Pin_1

custom parts:
  7-Segment LED I2C Backpack (red): 4-digit, 7-segment LED Display with I2C Control
  7-Segment LED I2C Backpack (green): 4-digit, 7-segment LED Display with I2C Control
  7-Segment LED I2C Backpack (yellow): 4-digit, 7-segment LED Display with I2C Control
